// Digital circuit counter.dig as structural Verilog
module counter (
  input  clk,
  input  start,
  input  rst,
  output endd
);

  wire and_1_out, and_2_out, not_1_out, not_3_out, not_4_out, not_5_out, not_6_out, not_7_out, not_8_out,
       or_1_out;
  wire [9:0] counter_1_out, not_2_out;

  not not_1 (not_1_out, rst);
  or or_1 (or_1_out, not_1_out, endd);
  Counter #(.Bits(10)) counter_1 (.en(start), .C(clk), .clr(or_1_out), .out(counter_1_out));  // open: ovf
  assign not_2_out = ~counter_1_out;  // Not not_2, 10 bits wide
  not not_3 (not_3_out, not_2_out[3]);
  not not_4 (not_4_out, not_2_out[5]);
  not not_5 (not_5_out, not_2_out[6]);
  not not_6 (not_6_out, not_2_out[7]);
  not not_7 (not_7_out, not_2_out[8]);
  not not_8 (not_8_out, not_2_out[9]);
  and and_1 (and_1_out, not_2_out[0], not_2_out[1], not_2_out[2], not_3_out, not_2_out[4]);
  and and_2 (and_2_out, not_4_out, not_5_out, not_6_out, not_7_out, not_8_out);
  and and_3 (endd, and_1_out, and_2_out);
endmodule
