// Digital circuit downcounter_new.dig as structural Verilog
module downcounter_new (
  input  EN,
  input  LOAD,
  input  CLK,
  input  RESET,
  input  [3:0] IN1,
  input  rst,
  output [3:0] CNT,
  output ZERO
);

  wire d_ff_as_1_nq, d_ff_as_2_nq, d_ff_as_3_nq, d_ff_as_4_nq, multiplexer_5_out, multiplexer_6_out,
       multiplexer_7_out, multiplexer_8_out, not_1_out;
  wire [0:0] and_1_out, and_2_out, and_3_out;
  wire [3:0] multiplexer_1_out;

  Multiplexer multiplexer_1 (.sel(rst), .in_0(IN1[0]), .in_1(1'b0), .out(multiplexer_1_out[0]));
  Multiplexer multiplexer_2 (.sel(rst), .in_0(IN1[1]), .in_1(1'b0), .out(multiplexer_1_out[1]));
  Multiplexer multiplexer_3 (.sel(rst), .in_0(IN1[2]), .in_1(1'b0), .out(multiplexer_1_out[2]));
  Multiplexer multiplexer_4 (.sel(rst), .in_0(IN1[3]), .in_1(1'b0), .out(multiplexer_1_out[3]));
  not not_1 (not_1_out, RESET);
  and and_1 (and_1_out[0], d_ff_as_1_nq, EN);
  and and_2 (and_2_out[0], d_ff_as_2_nq, and_1_out[0]);
  and and_3 (and_3_out[0], d_ff_as_3_nq, and_2_out[0]);
  Multiplexer #(.Selector_Bits(2)) multiplexer_5 (
    .sel({LOAD, EN}), .in_0(CNT[0]), .in_1(d_ff_as_1_nq), .in_2(multiplexer_1_out[0]),
    .in_3(multiplexer_1_out[0]), .out(multiplexer_5_out));
  Multiplexer #(.Selector_Bits(2)) multiplexer_6 (
    .sel({LOAD, and_1_out[0]}), .in_0(CNT[1]), .in_1(d_ff_as_2_nq), .in_2(multiplexer_1_out[1]),
    .in_3(multiplexer_1_out[1]), .out(multiplexer_6_out));
  Multiplexer #(.Selector_Bits(2)) multiplexer_7 (
    .sel({LOAD, and_2_out[0]}), .in_0(CNT[2]), .in_1(d_ff_as_3_nq), .in_2(multiplexer_1_out[2]),
    .in_3(multiplexer_1_out[2]), .out(multiplexer_7_out));
  Multiplexer #(.Selector_Bits(2)) multiplexer_8 (
    .sel({LOAD, and_3_out[0]}), .in_0(CNT[3]), .in_1(d_ff_as_4_nq), .in_2(multiplexer_1_out[3]),
    .in_3(multiplexer_1_out[3]), .out(multiplexer_8_out));
  D_FF_AS d_ff_as_1 (.Set(not_1_out), .D(multiplexer_5_out), .C(CLK), .Clr(1'b0), .Q(CNT[0]), .nQ(d_ff_as_1_nq));
  D_FF_AS d_ff_as_2 (.Set(not_1_out), .D(multiplexer_6_out), .C(CLK), .Clr(1'b0), .Q(CNT[1]), .nQ(d_ff_as_2_nq));
  D_FF_AS d_ff_as_3 (.Set(not_1_out), .D(multiplexer_7_out), .C(CLK), .Clr(1'b0), .Q(CNT[2]), .nQ(d_ff_as_3_nq));
  D_FF_AS d_ff_as_4 (.Set(not_1_out), .D(multiplexer_8_out), .C(CLK), .Clr(1'b0), .Q(CNT[3]), .nQ(d_ff_as_4_nq));
  and and_4 (ZERO, d_ff_as_4_nq, and_3_out[0]);
endmodule
